# Fritzing sketch Sensor Module Schematic (saved by Fritzing 0.9.10b)

parts:
  LCD_Display_-_20x4 = LCD-16X2 [package=lcd-16x2_noholes]
  ESP32_Microcontroller = Heltec WiFi LoRa 32 V2 [part_number=HTIT-WB32LA]
  Buzzer = Passive Buzzer
  MG-811_Gas_Sensor = Header 5 [package=1x05-1mm]
  Mute_Switch = SWITCH_SPDT [package=kps-1290]

nets:
  VSS: LCD_Display_-_20x4.VSS, ESP32_Microcontroller.GND, Buzzer.-, MG-811_Gas_Sensor.5
  N1: LCD_Display_-_20x4.VDD, ESP32_Microcontroller.pin_20, MG-811_Gas_Sensor.4
  N2: LCD_Display_-_20x4.RS, ESP32_Microcontroller.pin_32
  N3: LCD_Display_-_20x4.R_W, ESP32_Microcontroller.pin_33
  N4: LCD_Display_-_20x4.DB0, LCD_Display_-_20x4.DB1, LCD_Display_-_20x4.DB2, LCD_Display_-_20x4.DB3, LCD_Display_-_20x4.DB4, LCD_Display_-_20x4.DB5, LCD_Display_-_20x4.DB6, LCD_Display_-_20x4.DB7, LCD_Display_-_20x4.A, LCD_Display_-_20x4.K
  N5: ESP32_Microcontroller.pin_2, Mute_Switch.P
  N6: ESP32_Microcontroller.pin_14, MG-811_Gas_Sensor.2
  N7: Buzzer.S, Mute_Switch.S
